// Logisim project Lab02_Bool.circ as structural Verilog: 2 circuits, main circuit main
module main (
);


  // Notes on the sheet:
  //   Name
  //   Lab 02: Boolean Equations
  //   Date
endmodule

module Equation_1 (
);


  // Notes on the sheet:
  //   (A'BC')+(AB'C')+(ABC)
endmodule
