// Logisim project Lab03_Encoder.circ as structural Verilog
module main (
);


  // Notes on the sheet:
  //   Name
  //   Lab 03: Priority Encoder
  //   Date
endmodule
